# Fritzing sketch esp8266 (saved by Fritzing 0.9.3b)
breadboards: 1

parts:
  ESP8266 = NodeMCU V1.0
  M1 = DC Motor  # not connected
  M2 = DC Motor  # not connected
  M4 = DC Motor
  Motor_Driver = H-Bridge with L298N
  hc-sr1 = hc-sr04
  M3 = DC Motor
  Battery = Battery

nets:
  N1: ESP8266.D1, hc-sr1.Trig
  N2: ESP8266.D2, hc-sr1.Echo
  N3: ESP8266.D3, ESP8266.D4, ESP8266.D5, ESP8266.D7, ESP8266.D8, Motor_Driver.ENA, Motor_Driver.IN1, Motor_Driver.IN2, Motor_Driver.IN3, Motor_Driver.IN4
  3V3: ESP8266.3V3, hc-sr1.VCC
  GND: ESP8266.GND, Motor_Driver.GND, hc-sr1.GND, Battery.-
  N4: ESP8266.D6, Motor_Driver.ENB
  VIN: ESP8266.Vin, Motor_Driver.12V, Battery.+
  N5: M4.pin_1, Motor_Driver.M1-01
  N6: M4.pin_2, Motor_Driver.M1-02
  N7: Motor_Driver.M2-01, M3.pin_2
  N8: Motor_Driver.M2-02, M3.pin_1

custom parts:
  NodeMCU V1.0: ESP8266 based NodeMCU
  H-Bridge with L298N: h-bridge
  Battery: Your standard 2x 18650 battery pack (7,4 Volts)
